# Fritzing sketch door-sensor (saved by Fritzing 0.9.10b)
breadboards: 1

parts:
  IC1 = AE-TYBLE16 (300mil) [part_number=K-12339 package="DIP (Dual Inline) [THT]"]
  JP2 = Header 6 [package=1x06-smd-female-v2]
  C1 = Capacitor Polarized [package=cpol-radial-100uf-25v]
  Q1 = LTR-301 [package=ltr-301]
  R1 = Resistor [tolerance=±5% power=0.25 resistance=1k package=THT]
  BAT1 = Battery Holders [package=battcon_245mm]
  J1 = Screw terminal - 2 pins [package=THT]
  S1 = Toggle Switch [package=THT]
  S3 = Toggle Switch [package=THT]

nets:
  N1: IC1.DIP2, JP2.5
  N2: IC1.DIP3, JP2.4
  N3: IC1.DIP5, JP2.2
  N4: IC1.DIP6, JP2.1
  N5: IC1.DIP11, Q1.C, S1.L2
  N6: IC1.DIP13, JP2.3, C1.-, R1.Pin_1, BAT1.+, BAT1.-, J1.pin1
  N7: IC1.DIP14, JP2.6, C1.+, S3.COM
  N8: Q1.E, R1.Pin_0, S1.COM
  N9: J1.pin2, S3.L1

custom parts:
  AE-TYBLE16 (300mil): AE-TYBLE16 BLE module whose MPU core is nRF51822 as 300mil (7.62mm) breadfriendly width, actual width is 8.0mm
